// Logisim project music_player.circ as structural Verilog: 1 circuit, main circuit main
module main (
  input  ON_OFF
);

  wire and_1_out, and_2_out, and_3_out, and_4_out, and_5_out, and_6_out, and_7_out, and_8_out, and_9_out,
       and_10_out, and_11_out, and_12_out, and_13_out, and_14_out, and_15_out, and_16_out, and_17_out,
       and_18_out, and_19_out, and_20_out, and_21_out, and_22_out, and_23_out, and_24_out, and_25_out,
       and_26_out, and_27_out, and_28_out, and_29_out, and_30_out, and_31_out, and_32_out, and_33_out,
       and_34_out, and_35_out, and_36_out, and_37_out, and_39_out, and_41_out, and_42_out, and_43_out,
       and_44_out, and_45_out, and_46_out, buffer_1_out, buffer_2_out, buffer_3_out, buffer_4_out,
       buffer_5_out, buffer_6_out, buffer_7_out, buffer_8_out, buffer_9_out, buffer_10_out, buffer_11_out,
       buffer_12_out, buffer_13_out, buffer_14_out, buffer_15_out, buffer_16_out, buffer_17_out, d_ff_1_q,
       d_ff_2_q, d_ff_3_q, d_ff_4_q, d_ff_5_q, d_ff_6_q, d_ff_7_q, d_ff_8_q, d_ff_9_q, j_k_ff_1_q,
       j_k_ff_1_qn, j_k_ff_2_qn, j_k_ff_3_qn, j_k_ff_4_qn, j_k_ff_5_qn, j_k_ff_6_qn, j_k_ff_7_qn, next_out,
       NEXT_TRACK_out, nine2_out, nor_1_out, nor_2_out, not_1_out, not_2_out, not_3_out, not_4_out,
       not_5_out, not_6_out, not_7_out, not_8_out, not_9_out, not_10_out, not_11_out, not_12_out, not_13_out,
       not_14_out, not_15_out, not_16_out, not_17_out, not_18_out, not_19_out, not_20_out, not_21_out,
       not_22_out, not_23_out, not_24_out, one_out, or_1_out, or_2_out, or_3_out, or_4_out, or_5_out,
       or_6_out, or_7_out, or_8_out, or_9_out, or_10_out, or_11_out, or_12_out, or_13_out, or_14_out,
       or_15_out, or_16_out, or_17_out, or_18_out, or_19_out, or_20_out, or_21_out, or_22_out, or_23_out,
       or_24_out, or_25_out, PAUSE_out, PLAY_out, prev_out, PREV_TRACK_out, pulse_2_out, pulse_out,
       VOL_DOWN_out, VOL_UP_out;
  wire [3:0] and_38_out, and_40_out, j_k_ff_2_q, j_k_ff_3_q;

  Button PLAY (.out(PLAY_out));
  Button PAUSE (.out(PAUSE_out));
  Button VOL_UP (.out(VOL_UP_out));
  Button VOL_DOWN (.out(VOL_DOWN_out));
  Button NEXT_TRACK (.out(NEXT_TRACK_out));
  Button PREV_TRACK (.out(PREV_TRACK_out));
  and and_1 (and_1_out, PAUSE_out, d_ff_1_q);
  and and_2 (and_2_out, ON_OFF, PLAY_out);
  and and_3 (and_3_out, ON_OFF, and_1_out);
  not not_1 (not_1_out, VOL_UP_out);
  not not_2 (not_2_out, VOL_DOWN_out);
  or or_1 (or_1_out, and_2_out, and_3_out);
  or or_2 (or_2_out, not_1_out, VOL_DOWN_out);
  not not_3 (not_3_out, or_2_out);
  or or_3 (or_3_out, VOL_UP_out, not_2_out);
  buf buffer_1 (buffer_1_out, buffer_2_out);
  or or_4 (or_4_out, VOL_UP_out, VOL_DOWN_out);
  buf buffer_2 (buffer_2_out, or_4_out);
  nor nor_1 (nor_1_out, NEXT_TRACK_out, nor_2_out);
  nor nor_2 (nor_2_out, nor_1_out, PREV_TRACK_out);
  or or_5 (or_5_out, NEXT_TRACK_out, PREV_TRACK_out);
  D_Flip_Flop d_ff_1 (.D(and_2_out), .clk(buffer_3_out), .Q(d_ff_1_q), .reset(not_4_out));  // open: Qn, preset
  buf buffer_3 (buffer_3_out, and_2_out);
  J_K_Flip_Flop j_k_ff_1 (
    .J(or_1_out), .K(and_3_out), .clk(or_1_out), .Q(j_k_ff_1_q), .Qn(j_k_ff_1_qn), .reset(not_5_out));  // open: preset
  and and_4 (and_4_out, not_3_out, or_3_out);
  and and_5 (and_5_out, or_2_out, d_ff_3_q);
  buf buffer_4 (buffer_4_out, buffer_5_out);
  buf buffer_5 (buffer_5_out, buffer_7_out);
  buf buffer_6 (buffer_6_out, buffer_4_out);
  buf buffer_7 (buffer_7_out, buffer_1_out);
  buf buffer_8 (buffer_8_out, buffer_9_out);
  buf buffer_9 (buffer_9_out, nor_2_out);
  not not_4 (not_4_out, ON_OFF);
  not not_5 (not_5_out, ON_OFF);
  or or_6 (or_6_out, and_4_out, and_5_out);
  buf buffer_10 (buffer_10_out, buffer_6_out);
  buf buffer_11 (buffer_11_out, buffer_13_out);
  buf buffer_12 (buffer_12_out, buffer_14_out);
  buf buffer_13 (buffer_13_out, buffer_12_out);
  buf buffer_14 (buffer_14_out, buffer_8_out);
  not not_6 (not_6_out, j_k_ff_2_q[0]);
  not not_7 (not_7_out, j_k_ff_2_q[1]);
  not not_8 (not_8_out, j_k_ff_2_q[2]);
  not not_9 (not_9_out, j_k_ff_2_q[3]);
  and nine2 (nine2_out, not_6_out, not_7_out, not_8_out, not_9_out, not_10_out, not_11_out, not_12_out, not_13_out, not_14_out);
  not not_10 (not_10_out, buffer_16_out);
  not not_11 (not_11_out, j_k_ff_3_q[0]);
  not not_12 (not_12_out, j_k_ff_3_q[1]);
  not not_13 (not_13_out, j_k_ff_3_q[2]);
  not not_14 (not_14_out, j_k_ff_3_q[3]);
  not not_15 (not_15_out, buffer_16_out);
  D_Flip_Flop d_ff_2 (.D(or_6_out), .clk(and_6_out), .Q(d_ff_2_q));  // open: Qn, preset, reset
  and and_6 (and_6_out, buffer_10_out, ON_OFF);
  or or_7 (or_7_out, one_out, nine2_out);
  buf buffer_15 (buffer_15_out, buffer_11_out);
  buf buffer_16 (buffer_16_out, buffer_17_out);
  buf buffer_17 (buffer_17_out, buffer_15_out);
  or or_8 (or_8_out, pulse_2_out, and_7_out);
  and and_7 (and_7_out, pulse_out, not_15_out);
  and and_8 (and_8_out, ON_OFF, j_k_ff_1_q);
  and and_9 (and_9_out, j_k_ff_1_qn, ON_OFF);
  not not_16 (not_16_out, or_2_out);
  and and_10 (and_10_out, ON_OFF, d_ff_2_q);
  J_K_Flip_Flop #(.trigger("falling")) j_k_ff_2 (
    .J(ON_OFF), .K(ON_OFF), .clk(or_5_out), .Q(j_k_ff_2_q[0]), .Qn(j_k_ff_2_qn), .preset(or_7_out),
    .reset(next_out));
  J_K_Flip_Flop #(.trigger("falling")) j_k_ff_3 (
    .J(ON_OFF), .K(ON_OFF), .clk(or_8_out), .Q(j_k_ff_3_q[0]), .Qn(j_k_ff_3_qn), .reset(one_out));  // open: preset
  and and_11 (and_11_out, not_16_out, d_ff_2_q);
  and and_12 (and_12_out, or_2_out, d_ff_4_q);
  not not_17 (not_17_out, buffer_16_out);
  not not_18 (not_18_out, buffer_16_out);
  LED PLAY_2 (.in(and_8_out));
  LED PAUSE_2 (.in(and_9_out));
  or or_9 (or_9_out, and_11_out, and_12_out);
  and and_13 (and_13_out, buffer_16_out, j_k_ff_2_q[0]);
  and and_14 (and_14_out, j_k_ff_2_qn, not_17_out);
  and and_15 (and_15_out, buffer_16_out, j_k_ff_3_q[0]);
  and and_16 (and_16_out, j_k_ff_3_qn, not_18_out);
  D_Flip_Flop d_ff_3 (.D(or_9_out), .clk(and_6_out), .Q(d_ff_3_q));  // open: Qn, preset, reset
  and and_17 (and_17_out, ON_OFF, d_ff_3_q);
  J_K_Flip_Flop #(.trigger("falling")) j_k_ff_4 (
    .J(or_10_out), .K(or_10_out), .clk(or_5_out), .Q(j_k_ff_2_q[1]), .Qn(j_k_ff_4_qn), .reset(or_12_out));  // open: preset
  or or_10 (or_10_out, and_13_out, and_14_out);
  J_K_Flip_Flop #(.trigger("falling")) j_k_ff_5 (
    .J(or_11_out), .K(or_11_out), .clk(or_8_out), .Q(j_k_ff_3_q[1]), .Qn(j_k_ff_5_qn), .reset(or_13_out));  // open: preset
  or or_11 (or_11_out, and_15_out, and_16_out);
  not not_19 (not_19_out, or_2_out);
  and and_18 (and_18_out, not_19_out, d_ff_3_q);
  and and_19 (and_19_out, or_2_out, d_ff_5_q);
  or or_12 (or_12_out, prev_out, next_out);
  or or_13 (or_13_out, and_34_out, one_out);
  and and_20 (and_20_out, and_13_out, j_k_ff_2_q[1]);
  and and_21 (and_21_out, j_k_ff_4_qn, and_14_out);
  and and_22 (and_22_out, and_15_out, j_k_ff_3_q[1]);
  and and_23 (and_23_out, j_k_ff_5_qn, and_16_out);
  D_Flip_Flop d_ff_4 (.D(or_14_out), .clk(and_6_out), .Q(d_ff_4_q));  // open: Qn, preset, reset
  or or_14 (or_14_out, and_18_out, and_19_out);
  or or_15 (or_15_out, and_20_out, and_21_out);
  or or_16 (or_16_out, and_22_out, and_23_out);
  not not_20 (not_20_out, or_2_out);
  and and_24 (and_24_out, ON_OFF, d_ff_4_q);
  J_K_Flip_Flop #(.trigger("falling")) j_k_ff_6 (
    .J(or_15_out), .K(or_15_out), .clk(or_5_out), .Q(j_k_ff_2_q[2]), .Qn(j_k_ff_6_qn), .reset(or_17_out));  // open: preset
  or or_17 (or_17_out, prev_out, next_out);
  J_K_Flip_Flop #(.trigger("falling")) j_k_ff_7 (
    .J(or_16_out), .K(or_16_out), .clk(or_8_out), .Q(j_k_ff_3_q[2]), .Qn(j_k_ff_7_qn), .reset(or_18_out));  // open: preset
  or or_18 (or_18_out, and_34_out, one_out);
  and and_25 (and_25_out, not_20_out, d_ff_4_q);
  and and_26 (and_26_out, or_2_out, d_ff_6_q);
  and and_27 (and_27_out, and_20_out, j_k_ff_2_q[2]);
  and and_28 (and_28_out, j_k_ff_6_qn, and_21_out);
  and and_29 (and_29_out, and_22_out, j_k_ff_3_q[2]);
  and and_30 (and_30_out, j_k_ff_7_qn, and_23_out);
  or or_19 (or_19_out, and_25_out, and_26_out);
  D_Flip_Flop d_ff_5 (.D(or_19_out), .clk(and_6_out), .Q(d_ff_5_q));  // open: Qn, preset, reset
  J_K_Flip_Flop #(.trigger("falling")) j_k_ff_8 (
    .J(or_20_out), .K(or_20_out), .clk(or_5_out), .Q(j_k_ff_2_q[3]), .preset(nine2_out), .reset(next_out));  // open: Qn
  or or_20 (or_20_out, and_27_out, and_28_out);
  J_K_Flip_Flop #(.trigger("falling")) j_k_ff_9 (
    .J(or_21_out), .K(or_21_out), .clk(or_8_out), .Q(j_k_ff_3_q[3]), .reset(one_out));  // open: Qn, preset
  or or_21 (or_21_out, and_29_out, and_30_out);
  not not_21 (not_21_out, or_2_out);
  and and_31 (and_31_out, ON_OFF, d_ff_5_q);
  LED led_1 (.in(and_10_out));
  and and_32 (and_32_out, not_21_out, d_ff_5_q);
  and and_33 (and_33_out, or_2_out, d_ff_7_q);
  LED led_2 (.in(and_35_out));
  LED led_3 (.in(and_24_out));
  LED led_4 (.in(and_17_out));
  LED led_5 (.in(and_31_out));
  and next (next_out, j_k_ff_2_q[3], buffer_16_out, j_k_ff_2_q[1]);
  and one (one_out, j_k_ff_3_q[3], buffer_16_out, j_k_ff_3_q[1]);
  or or_22 (or_22_out, and_32_out, and_33_out);
  LED led_6 (.in(and_46_out));
  LED led_7 (.in(and_43_out));
  LED led_8 (.in(and_39_out));
  and prev (prev_out, j_k_ff_2_q[3], j_k_ff_2_q[2], j_k_ff_2_q[1], j_k_ff_2_q[0]);
  and and_34 (and_34_out, j_k_ff_3_q[3], j_k_ff_3_q[2], j_k_ff_3_q[1], j_k_ff_3_q[0]);
  D_Flip_Flop d_ff_6 (.D(or_22_out), .clk(and_6_out), .Q(d_ff_6_q));  // open: Qn, preset, reset
  and and_35 (and_35_out, ON_OFF, d_ff_6_q);
  nor pulse (pulse_out, j_k_ff_2_q[0], j_k_ff_2_q[1], j_k_ff_2_q[2], j_k_ff_2_q[3]);
  not not_22 (not_22_out, or_2_out);
  and pulse_2 (pulse_2_out, j_k_ff_2_q[0], buffer_16_out, j_k_ff_2_q[3]);
  and and_36 (and_36_out, not_22_out, d_ff_6_q);
  and and_37 (and_37_out, or_2_out, d_ff_8_q);
  D_Flip_Flop d_ff_7 (.D(or_23_out), .clk(and_6_out), .Q(d_ff_7_q));  // open: Qn, preset, reset
  or or_23 (or_23_out, and_36_out, and_37_out);
  Hex_Digit_Display hex_digit_display_1 (.value(and_38_out));  // open: dp
  Hex_Digit_Display hex_digit_display_2 (.value(and_40_out));  // open: dp
  assign and_38_out = j_k_ff_3_q & {4{ON_OFF}};  // AND_Gate and_38, 4 bits wide
  and and_39 (and_39_out, ON_OFF, d_ff_7_q);
  assign and_40_out = {4{ON_OFF}} & j_k_ff_2_q;  // AND_Gate and_40, 4 bits wide
  not not_23 (not_23_out, or_2_out);
  and and_41 (and_41_out, not_23_out, d_ff_7_q);
  and and_42 (and_42_out, or_2_out, d_ff_9_q);
  D_Flip_Flop d_ff_8 (.D(or_24_out), .clk(and_6_out), .Q(d_ff_8_q));  // open: Qn, preset, reset
  or or_24 (or_24_out, and_41_out, and_42_out);
  not not_24 (not_24_out, or_2_out);
  and and_43 (and_43_out, ON_OFF, d_ff_8_q);
  and and_44 (and_44_out, not_24_out, d_ff_8_q);
  and and_45 (and_45_out, or_2_out, or_3_out);
  or or_25 (or_25_out, and_44_out, and_45_out);
  D_Flip_Flop d_ff_9 (.D(or_25_out), .clk(and_6_out), .Q(d_ff_9_q));  // open: Qn, preset, reset
  and and_46 (and_46_out, ON_OFF, d_ff_9_q);

  // Notes on the sheet:
  //   VOLUME
  //   TRACK
endmodule
