// Logisim project play_pause.circ as structural Verilog: 1 circuit, main circuit main
module main (
  input  ON_OFF
);

  wire and_1_out, and_2_out, and_3_out, and_4_out, and_5_out, buffer_1_out, d_ff_1_q, j_k_ff_1_q,
       j_k_ff_1_qn, not_1_out, not_2_out, or_1_out, PAUSE_out, PLAY_out;

  Button PLAY (.out(PLAY_out));
  Button PAUSE (.out(PAUSE_out));
  and and_1 (and_1_out, PAUSE_out, d_ff_1_q);
  and and_2 (and_2_out, ON_OFF, PLAY_out);
  and and_3 (and_3_out, ON_OFF, and_1_out);
  or or_1 (or_1_out, and_2_out, and_3_out);
  D_Flip_Flop d_ff_1 (.D(and_2_out), .clk(buffer_1_out), .Q(d_ff_1_q), .reset(not_1_out));  // open: Qn, preset
  buf buffer_1 (buffer_1_out, and_2_out);
  not not_1 (not_1_out, ON_OFF);
  J_K_Flip_Flop j_k_ff_1 (
    .J(or_1_out), .K(and_3_out), .clk(or_1_out), .Q(j_k_ff_1_q), .Qn(j_k_ff_1_qn), .reset(not_2_out));  // open: preset
  not not_2 (not_2_out, ON_OFF);
  and and_4 (and_4_out, ON_OFF, j_k_ff_1_q);
  and and_5 (and_5_out, j_k_ff_1_qn, ON_OFF);
  LED PLAY_2 (.in(and_4_out));
  LED PAUSE_2 (.in(and_5_out));
endmodule
