// Logisim project volume.circ as structural Verilog: 1 circuit, main circuit main
module main (
  input  ON_OFF
);

  wire and_1_out, and_2_out, and_3_out, and_4_out, and_5_out, and_6_out, and_7_out, and_8_out, and_9_out,
       and_10_out, and_11_out, and_12_out, and_13_out, and_14_out, and_15_out, and_16_out, and_17_out,
       and_18_out, and_19_out, and_20_out, and_21_out, and_22_out, and_23_out, and_24_out, and_25_out,
       buffer_1_out, buffer_2_out, buffer_3_out, buffer_4_out, buffer_5_out, buffer_6_out, buffer_7_out,
       d_ff_1_q, d_ff_2_q, d_ff_3_q, d_ff_4_q, d_ff_5_q, d_ff_6_q, d_ff_7_q, d_ff_8_q, not_1_out, not_2_out,
       not_3_out, not_4_out, not_5_out, not_6_out, not_7_out, not_8_out, not_9_out, not_10_out, or_1_out,
       or_2_out, or_3_out, or_4_out, or_5_out, or_6_out, or_7_out, or_8_out, or_9_out, or_10_out, or_11_out,
       VOL_DOWN_out, VOL_UP_out;

  Button VOL_UP (.out(VOL_UP_out));
  Button VOL_DOWN (.out(VOL_DOWN_out));
  not not_1 (not_1_out, VOL_UP_out);
  not not_2 (not_2_out, VOL_DOWN_out);
  or or_1 (or_1_out, not_1_out, VOL_DOWN_out);
  or or_2 (or_2_out, VOL_UP_out, not_2_out);
  or or_3 (or_3_out, VOL_UP_out, VOL_DOWN_out);
  not not_3 (not_3_out, or_1_out);
  buf buffer_1 (buffer_1_out, buffer_4_out);
  buf buffer_2 (buffer_2_out, buffer_3_out);
  buf buffer_3 (buffer_3_out, or_3_out);
  buf buffer_4 (buffer_4_out, buffer_2_out);
  and and_1 (and_1_out, not_3_out, or_2_out);
  and and_2 (and_2_out, or_1_out, d_ff_2_q);
  buf buffer_5 (buffer_5_out, buffer_6_out);
  buf buffer_6 (buffer_6_out, buffer_7_out);
  buf buffer_7 (buffer_7_out, buffer_1_out);
  D_Flip_Flop d_ff_1 (.D(or_4_out), .clk(and_3_out), .Q(d_ff_1_q));  // open: Qn, preset, reset
  or or_4 (or_4_out, and_1_out, and_2_out);
  and and_3 (and_3_out, buffer_5_out, ON_OFF);
  not not_4 (not_4_out, or_1_out);
  and and_4 (and_4_out, ON_OFF, d_ff_1_q);
  and and_5 (and_5_out, not_4_out, d_ff_1_q);
  and and_6 (and_6_out, or_1_out, d_ff_3_q);
  or or_5 (or_5_out, and_5_out, and_6_out);
  D_Flip_Flop d_ff_2 (.D(or_5_out), .clk(and_3_out), .Q(d_ff_2_q));  // open: Qn, preset, reset
  not not_5 (not_5_out, or_1_out);
  and and_7 (and_7_out, ON_OFF, d_ff_2_q);
  and and_8 (and_8_out, not_5_out, d_ff_2_q);
  and and_9 (and_9_out, or_1_out, d_ff_4_q);
  or or_6 (or_6_out, and_8_out, and_9_out);
  D_Flip_Flop d_ff_3 (.D(or_6_out), .clk(and_3_out), .Q(d_ff_3_q));  // open: Qn, preset, reset
  and and_10 (and_10_out, ON_OFF, d_ff_3_q);
  not not_6 (not_6_out, or_1_out);
  and and_11 (and_11_out, not_6_out, d_ff_3_q);
  and and_12 (and_12_out, or_1_out, d_ff_5_q);
  D_Flip_Flop d_ff_4 (.D(or_7_out), .clk(and_3_out), .Q(d_ff_4_q));  // open: Qn, preset, reset
  or or_7 (or_7_out, and_11_out, and_12_out);
  not not_7 (not_7_out, or_1_out);
  and and_13 (and_13_out, ON_OFF, d_ff_4_q);
  and and_14 (and_14_out, not_7_out, d_ff_4_q);
  and and_15 (and_15_out, or_1_out, d_ff_6_q);
  LED led_1 (.in(and_7_out));
  LED led_2 (.in(and_10_out));
  LED led_3 (.in(and_4_out));
  or or_8 (or_8_out, and_14_out, and_15_out);
  LED led_4 (.in(and_13_out));
  LED led_5 (.in(and_16_out));
  LED led_6 (.in(and_19_out));
  LED led_7 (.in(and_22_out));
  D_Flip_Flop d_ff_5 (.D(or_8_out), .clk(and_3_out), .Q(d_ff_5_q));  // open: Qn, preset, reset
  and and_16 (and_16_out, ON_OFF, d_ff_5_q);
  LED led_8 (.in(and_25_out));
  not not_8 (not_8_out, or_1_out);
  and and_17 (and_17_out, not_8_out, d_ff_5_q);
  and and_18 (and_18_out, or_1_out, d_ff_7_q);
  or or_9 (or_9_out, and_17_out, and_18_out);
  D_Flip_Flop d_ff_6 (.D(or_9_out), .clk(and_3_out), .Q(d_ff_6_q));  // open: Qn, preset, reset
  and and_19 (and_19_out, ON_OFF, d_ff_6_q);
  not not_9 (not_9_out, or_1_out);
  and and_20 (and_20_out, not_9_out, d_ff_6_q);
  and and_21 (and_21_out, or_1_out, d_ff_8_q);
  or or_10 (or_10_out, and_20_out, and_21_out);
  D_Flip_Flop d_ff_7 (.D(or_10_out), .clk(and_3_out), .Q(d_ff_7_q));  // open: Qn, preset, reset
  and and_22 (and_22_out, ON_OFF, d_ff_7_q);
  not not_10 (not_10_out, or_1_out);
  and and_23 (and_23_out, not_10_out, d_ff_7_q);
  and and_24 (and_24_out, or_1_out, or_2_out);
  D_Flip_Flop d_ff_8 (.D(or_11_out), .clk(and_3_out), .Q(d_ff_8_q));  // open: Qn, preset, reset
  or or_11 (or_11_out, and_23_out, and_24_out);
  and and_25 (and_25_out, ON_OFF, d_ff_8_q);

  // Notes on the sheet:
  //   VOLUME
endmodule
