// Logisim project half_adder.circ as structural Verilog: 1 circuit, main circuit main
module main (
  input  input_1,
  input  input_2
);

  wire and_1_out, xor_1_out;

  xor xor_1 (xor_1_out, input_1, input_2);
  and and_1 (and_1_out, input_2, input_1);
  LED led_1 (.in(xor_1_out));
  LED led_2 (.in(and_1_out));

  // Notes on the sheet:
  //   sum output
  //   carry output
endmodule
