// Logisim project 4bit_adder.circ as structural Verilog: 1 circuit, main circuit main
module main (
  input  input_a1,
  input  input_b1,
  input  input_a2,
  input  input_b2,
  input  input_a3,
  input  input_b3,
  input  input_a4,
  input  input_b4
);

  wire and_1_out, and_2_out, and_3_out, and_4_out, and_5_out, and_6_out, and_7_out, or_1_out, or_2_out,
       or_3_out, xor_1_out, xor_2_out, xor_3_out, xor_4_out, xor_5_out, xor_6_out, xor_7_out;

  xor xor_1 (xor_1_out, input_a2, input_b2);
  xor xor_2 (xor_2_out, input_a3, input_b3);
  xor xor_3 (xor_3_out, input_a4, input_b4);
  xor xor_4 (xor_4_out, input_a1, input_b1);
  and and_1 (and_1_out, input_b1, input_a1);
  and and_2 (and_2_out, input_b2, input_a2);
  and and_3 (and_3_out, input_b3, input_a3);
  and and_4 (and_4_out, input_b4, input_a4);
  xor xor_5 (xor_5_out, and_1_out, xor_1_out);
  and and_5 (and_5_out, and_1_out, xor_1_out);
  xor xor_6 (xor_6_out, or_1_out, xor_2_out);
  and and_6 (and_6_out, or_1_out, xor_2_out);
  xor xor_7 (xor_7_out, or_2_out, xor_3_out);
  and and_7 (and_7_out, or_2_out, xor_3_out);
  or or_1 (or_1_out, and_5_out, and_2_out);
  or or_2 (or_2_out, and_6_out, and_3_out);
  or or_3 (or_3_out, and_7_out, and_4_out);
  LED led_1 (.in(xor_4_out));
  LED led_2 (.in(and_1_out));
  LED led_3 (.in(xor_5_out));
  LED led_4 (.in(or_1_out));
  LED led_5 (.in(xor_6_out));
  LED led_6 (.in(or_2_out));
  LED led_7 (.in(xor_7_out));
  LED led_8 (.in(or_3_out));

  // Notes on the sheet:
  //   sum output 1
  //   carry output 1
  //   sum output 2
  //   carry output 2
  //   sum output 3
  //   carry output 3
  //   sum output 4
  //   carry output 4
endmodule
