// Logisim project 3_bit_ripple_counter.circ as structural Verilog: 1 circuit, main circuit main
module main (
  input  in_1,
  input  in_2
);

  wire clock_1_out;
  wire [2:0] j_k_ff_3_q;

  Clock clock_1 (.out(clock_1_out));
  J_K_Flip_Flop #(.trigger("falling")) j_k_ff_1 (
    .J(in_1), .K(in_1), .clk(j_k_ff_3_q[1]), .Q(j_k_ff_3_q[2]));  // open: Qn, preset, reset
  J_K_Flip_Flop #(.trigger("falling")) j_k_ff_2 (
    .J(in_1), .K(in_1), .clk(j_k_ff_3_q[0]), .Q(j_k_ff_3_q[1]));  // open: Qn, preset, reset
  J_K_Flip_Flop #(.trigger("falling")) j_k_ff_3 (
    .J(in_1), .K(in_1), .clk(clock_1_out), .Q(j_k_ff_3_q[0]));  // open: Qn, preset, reset
  Hex_Digit_Display hex_digit_display_1 (.value({in_2, j_k_ff_3_q}));  // open: dp
endmodule
