// Logisim project MOD6.circ as structural Verilog: 1 circuit, main circuit main
module main (
  input  in_1,
  input  in_2,
  input  in_3
);

  wire and_1_out, and_2_out, and_3_out, and_4_out, clock_1_out, clock_2_out, j_k_ff_2_q, j_k_ff_4_q,
       j_k_ff_6_q;
  wire [2:0] j_k_ff_1_q;

  Clock clock_1 (.out(clock_1_out));
  Clock clock_2 (.out(clock_2_out));
  J_K_Flip_Flop j_k_ff_1 (
    .J(in_1), .K(in_1), .clk(clock_1_out), .Q(j_k_ff_1_q[0]), .reset(and_3_out));  // open: Qn, preset
  J_K_Flip_Flop j_k_ff_2 (
    .J(in_3), .K(in_3), .clk(clock_2_out), .Q(j_k_ff_2_q), .reset(and_4_out));  // open: Qn, preset
  J_K_Flip_Flop j_k_ff_3 (
    .J(j_k_ff_1_q[0]), .K(j_k_ff_1_q[0]), .clk(clock_1_out), .Q(j_k_ff_1_q[1]), .reset(and_3_out));  // open: Qn, preset
  J_K_Flip_Flop j_k_ff_4 (
    .J(j_k_ff_2_q), .K(j_k_ff_2_q), .clk(clock_2_out), .Q(j_k_ff_4_q), .reset(and_4_out));  // open: Qn, preset
  LED led_1 (.in(j_k_ff_2_q));
  LED led_2 (.in(j_k_ff_4_q));
  and and_1 (and_1_out, j_k_ff_1_q[0], j_k_ff_1_q[1]);
  J_K_Flip_Flop j_k_ff_5 (
    .J(and_1_out), .K(and_1_out), .clk(clock_1_out), .Q(j_k_ff_1_q[2]), .reset(and_3_out));  // open: Qn, preset
  and and_2 (and_2_out, j_k_ff_2_q, j_k_ff_4_q);
  J_K_Flip_Flop j_k_ff_6 (
    .J(and_2_out), .K(and_2_out), .clk(clock_2_out), .Q(j_k_ff_6_q), .reset(and_4_out));  // open: Qn, preset
  LED led_3 (.in(j_k_ff_6_q));
  and and_3 (and_3_out, j_k_ff_1_q[2], j_k_ff_1_q[1]);
  and and_4 (and_4_out, j_k_ff_6_q, j_k_ff_4_q);
  Hex_Digit_Display hex_digit_display_1 (.value({in_2, j_k_ff_1_q}));  // open: dp
endmodule
