// Logisim project register.circ as structural Verilog: 1 circuit, main circuit main
module main (
  input  in_1,
  input  in_2,
  input  in_3,
  input  in_4
);

  wire clock_1_out, d_ff_1_q, d_ff_2_q, d_ff_3_q, d_ff_4_q;

  Clock clock_1 (.out(clock_1_out));
  D_Flip_Flop d_ff_1 (.D(clock_1_out), .clk(in_1), .Q(d_ff_1_q));  // open: Qn, preset, reset
  LED led_1 (.in(d_ff_1_q));
  D_Flip_Flop d_ff_2 (.D(clock_1_out), .clk(in_2), .Q(d_ff_2_q));  // open: Qn, preset, reset
  LED led_2 (.in(d_ff_2_q));
  D_Flip_Flop d_ff_3 (.D(clock_1_out), .clk(in_3), .Q(d_ff_3_q));  // open: Qn, preset, reset
  LED led_3 (.in(d_ff_3_q));
  D_Flip_Flop d_ff_4 (.D(clock_1_out), .clk(in_4), .Q(d_ff_4_q));  // open: Qn, preset, reset
  LED led_4 (.in(d_ff_4_q));
endmodule
