// Logisim project 2_bit_encoder.circ as structural Verilog: 1 circuit, main circuit main
module main (
  input  in_1,
  input  in_2
);

  wire or_1_out;

  or or_1 (or_1_out, in_1, in_2);
  LED led_1 (.in(or_1_out));
endmodule
